# Fritzing sketch Wemos_DS18B20 (saved by Fritzing 0.9.3b)
circuit board: 8.46667cm x 5.64444cm
breadboards: 1

parts:
  WeMos_D1_Mini1 = WeMos D1 Mini
  DS1 = DS18B20 1-Wire Temperature Sensor [part_number=DS18B20]

nets:
  3V3: WeMos_D1_Mini1.3V3, DS1.VDD
  N1: WeMos_D1_Mini1.D2, DS1.DQ
  N2: WeMos_D1_Mini1.G, DS1.GND
